// Logisim project JZ101.circ as structural Verilog: 8 circuits, main circuit main
module main (
  input  in_1
);

  wire button_1_out, button_2_out, button_3_out, clock_1_out, cpu_jz_101_1_db_enabled, cpu_jz_101_1_halted,
       cpu_jz_101_1_load_mem, io_con_1_write_key, io_con_1_write_ram, io_con_1_write_term;
  wire [6:0] io_con_1_term_out, keyboard_1_data;
  wire [15:0] cpu_jz_101_1_addr_out, cpu_jz_101_1_fr, cpu_jz_101_1_out, cpu_jz_101_1_r1, cpu_jz_101_1_r2,
       cpu_jz_101_1_sp, io_con_1_data_out, ram_1_data;

  Clock clock_1 (.out(clock_1_out));
  Button button_1 (.out(button_1_out));
  Button button_2 (.out(button_2_out));
  LED led_1 (.in(cpu_jz_101_1_db_enabled));
  LED led_2 (.in(cpu_jz_101_1_halted));
  CPU_JZ_101 cpu_jz_101_1 (
    .Clock(clock_1_out), .Inurupt(in_1), .Next_ins(button_1_out), .TogDB(button_2_out),
    .DB_Enabled(cpu_jz_101_1_db_enabled), .Halted(cpu_jz_101_1_halted), .FR(cpu_jz_101_1_fr),
    .SP(cpu_jz_101_1_sp), .R1(cpu_jz_101_1_r1), .R2(cpu_jz_101_1_r2), .LOAD_MEM(cpu_jz_101_1_load_mem),
    .ADDR_OUT(cpu_jz_101_1_addr_out), .IN(io_con_1_data_out), .OUT(cpu_jz_101_1_out));
  // Probe on cpu_jz_101_1_fr
  // Probe on cpu_jz_101_1_sp
  // Probe on cpu_jz_101_1_r1
  // Probe on cpu_jz_101_1_r2
  IO_CON io_con_1 (
    .DATA_OUT(io_con_1_data_out), .DATA_IN(cpu_jz_101_1_out), .WRITE_TERm(io_con_1_write_term),
    .WRITE_KEY(io_con_1_write_key), .CPU_SIG(cpu_jz_101_1_load_mem), .ADDR_IN(cpu_jz_101_1_addr_out),
    .WRITE_RAM(io_con_1_write_ram), .TERM_OUT(io_con_1_term_out), .KEY_IN(keyboard_1_data),
    .RAM_IN(ram_1_data));  // open: WRITE_INT, WRITE_MASK, INTURIN
  TTY tty_1 (.data(io_con_1_term_out), .clk(io_con_1_write_term), .we(1'b1), .clr(button_3_out));
  Button button_3 (.out(button_3_out));
  Keyboard keyboard_1 (.clk(io_con_1_write_key), .re(1'b1), .data(keyboard_1_data));  // open: clr, avail
  RAM #(.addrWidth(16), .dataWidth(16), .bus("separate")) ram_1 (
    .addr(cpu_jz_101_1_addr_out), .din(cpu_jz_101_1_out), .data(ram_1_data), .str(1'b1), .sel(1'b1),
    .clk(io_con_1_write_ram), .ld(1'b1));  // open: clr

  // Notes on the sheet:
  //   DB Enabled
  //   Debug Step
  //   Toggle DB
  //   Halted
endmodule

module CPU_JZ_101 (
  input  [15:0] IN,
  input  Clock,
  input  Inurupt,
  input  Next_ins,
  input  TogDB,
  output [15:0] FR,
  output [15:0] SP,
  output [15:0] R1,
  output [15:0] R2,
  output [15:0] OUT,
  output DB_Enabled,
  output Halted,
  output [15:0] ADDR_OUT,
  output LOAD_MEM
);

  wire DEST_ADDR, FLAGS_ALU, JMP_W_FLAGS, JUMP, LOAD_DEST, LOAD_FLAGS, LOAD_INS, LOAD_OPRAND, LOAD_PC,
       MATH_WITH_OP, PC_2, PC___1, PC_ISR, SP___1, SP_t, SRC_ADDR;
  wire [3:0] DB_SELECT;
  wire [15:0] ALU_ans, ALU_flag_out, INS_REG_q, multiplexer_2_out, OPRAND_REG_q, PC_q, pc_select_1_pc_out,
       reges_1_dest_out, reges_1_src_out;

  Multiplexer #(.select(4), .width(16)) multiplexer_1 (
    .in0(IN), .in1(reges_1_src_out), .in2(reges_1_dest_out), .in3(SP), .in4(ALU_ans), .in5(OPRAND_REG_q),
    .in6(PC_q), .in7(INS_REG_q), .out(OUT), .sel(DB_SELECT));  // open: in8, in9, in10, in11, in12, in13, in14, in15, en
  CONTROL control_1 (
    .LOAD_PC(LOAD_PC), .LOAD_MEM(LOAD_MEM), .LOAD_DEST(LOAD_DEST), .LOAD_FLAGS(LOAD_FLAGS),
    .LOAD_OPRAND(LOAD_OPRAND), .LOAD_INS(LOAD_INS), .ALU_TO_FLAG(FLAGS_ALU), .OPRAND_TO_ALU(MATH_WITH_OP),
    .PC___1_TO_ADDR(PC___1), .SP_TO_ADR(SP_t), .SP___1_TO_ADR(SP___1), .SRC_TO_ADR(SRC_ADDR),
    .DEST_TO_ADR(DEST_ADDR), .PC_TO_DB(JUMP), .PC_TO_DB_W_F(JMP_W_FLAGS), .INS_IN(OUT),
    .DB_SELECT(DB_SELECT), .PC___2(PC_2), .CLOCK(Clock), .Inturupt(Inurupt), .next_ins(Next_ins),
    .Toggle_DB(TogDB), .DB_ENABLED(DB_Enabled), .Halted(Halted), .PC_ISR(PC_ISR));
  Register #(.width(16)) INS_REG (.D(OUT), .Q(INS_REG_q), .clk(LOAD_INS));  // open: en, clr
  Register #(.width(16)) OPRAND_REG (.D(OUT), .Q(OPRAND_REG_q), .clk(LOAD_OPRAND));  // open: en, clr
  Multiplexer #(.width(16)) multiplexer_2 (
    .in0(reges_1_dest_out), .in1(OPRAND_REG_q), .out(multiplexer_2_out), .sel(MATH_WITH_OP));  // open: en
  ALU ALU (
    .X(reges_1_src_out), .Y(multiplexer_2_out), .INS(INS_REG_q), .FLAG_IN(FR), .ANS(ALU_ans),
    .FLAG_OUT(ALU_flag_out));
  ADRR_SELECT adrr_select_1 (
    .PC___1(PC___1), .SRC_IN_2(SRC_ADDR), .DEST_IN_2(DEST_ADDR), .SP_IN_2(SP_t), .SP__1(SP___1),
    .PC_IN(PC_q), .OP_IN(OPRAND_REG_q), .SRC_IN(reges_1_src_out), .DEST_IN(reges_1_dest_out), .SP_IN(SP),
    .OUT_ADDR(ADDR_OUT));
  REGES reges_1 (
    .INS_IN(INS_REG_q), .Write_DEST(LOAD_DEST), .SET_F_TO_ALU(FLAGS_ALU), .WRITE_FLAG(LOAD_FLAGS),
    .DB_IN(OUT), .R1(R1), .R2(R2), .FLAGS_IN(ALU_flag_out), .FLAGS_OUT(FR), .SP_OUT(SP),
    .SRC_OUT(reges_1_src_out), .DEST_OUT(reges_1_dest_out));
  PC_SELECT pc_select_1 (
    .PC_IN(PC_q), .INS_IN(INS_REG_q), .FLAGS_IN(FR), .JMP(JMP_W_FLAGS), .DJ(JUMP), .PC_2(PC_2),
    .PC_ISR(PC_ISR), .DB_IN(OUT), .PC_OUT(pc_select_1_pc_out));
  Register #(.width(16)) PC (.D(pc_select_1_pc_out), .Q(PC_q), .clk(LOAD_PC));  // open: en, clr

  // Notes on the sheet:
  //   Data Bus
  //   The chip to the right with lots of wires leading in and out is the register bank. 
  //   The device next to the PC is the logic for deciding what the next PC value. 
  //   The device near the bottom with lots of wires leading into the top and one 
  //   Out of the bottom is logic for deciding the output to the address bus. 
  //   The long device near the bottom in the control unit. The brains of the brain. 
  //   This is the CPU. For simplicity most digital logic has been moved into sub_curcits. 
endmodule

module REGES (
  input  [15:0] DB_IN,
  input  [15:0] INS_IN,
  input  Write_DEST,
  input  SET_F_TO_ALU,
  input  WRITE_FLAG,
  input  [15:0] FLAGS_IN,
  output [15:0] R1,
  output [15:0] R2,
  output [15:0] SRC_OUT,
  output [15:0] DEST_OUT,
  output [15:0] FLAGS_OUT,
  output [15:0] SP_OUT
);

  wire and_1_out, and_2_out, and_3_out, and_4_out, and_5_out, and_6_out, and_7_out, and_8_out, and_9_out,
       and_10_out, and_11_out, and_12_out, and_13_out, and_14_out, and_15_out, and_16_out, decoder_1_out0,
       decoder_1_out1, decoder_1_out2, decoder_1_out3, decoder_2_out0, decoder_2_out1, decoder_2_out2,
       decoder_2_out3, or_1_out;
  wire [15:0] multiplexer_1_out, register_1_q, register_2_q, register_3_q, register_5_q, register_6_q,
       register_7_q, register_9_q, register_10_q, register_12_q, register_13_q, register_14_q;

  Decoder #(.select(2)) decoder_1 (
    .out0(decoder_1_out0), .out1(decoder_1_out1), .out2(decoder_1_out2), .out3(decoder_1_out3),
    .sel(INS_IN[3:2]));  // open: en
  and and_1 (and_1_out, decoder_2_out0, decoder_1_out1);
  and and_2 (and_2_out, decoder_2_out0, decoder_1_out2);
  and and_3 (and_3_out, decoder_2_out0, decoder_1_out3);
  Register #(.width(16)) register_1 (.D(DB_IN), .en(and_1_out), .Q(register_1_q), .clk(Write_DEST));  // open: clr
  Register #(.width(16)) register_2 (.D(DB_IN), .en(and_2_out), .Q(register_2_q), .clk(Write_DEST));  // open: clr
  Register #(.width(16)) register_3 (.D(DB_IN), .en(and_3_out), .Q(register_3_q), .clk(Write_DEST));  // open: clr
  Decoder #(.select(2)) decoder_2 (
    .out0(decoder_2_out0), .out1(decoder_2_out1), .out2(decoder_2_out2), .out3(decoder_2_out3),
    .sel(INS_IN[1:0]));  // open: en
  and and_4 (and_4_out, decoder_2_out1, decoder_1_out0);
  and and_5 (and_5_out, decoder_2_out1, decoder_1_out1);
  and and_6 (and_6_out, decoder_2_out1, decoder_1_out2);
  and and_7 (and_7_out, decoder_2_out1, decoder_1_out3);
  Register #(.width(16)) register_4 (.D(DB_IN), .en(and_4_out), .Q(R1), .clk(Write_DEST));  // open: clr
  and and_8 (and_8_out, decoder_2_out2, decoder_1_out0);
  Register #(.width(16)) register_5 (.D(DB_IN), .en(and_5_out), .Q(register_5_q), .clk(Write_DEST));  // open: clr
  and and_9 (and_9_out, decoder_2_out2, decoder_1_out1);
  Register #(.width(16)) register_6 (.D(DB_IN), .en(and_6_out), .Q(register_6_q), .clk(Write_DEST));  // open: clr
  and and_10 (and_10_out, decoder_2_out2, decoder_1_out2);
  Register #(.width(16)) register_7 (.D(DB_IN), .en(and_7_out), .Q(register_7_q), .clk(Write_DEST));  // open: clr
  and and_11 (and_11_out, decoder_2_out2, decoder_1_out3);
  Register #(.width(16)) register_8 (.D(DB_IN), .en(and_8_out), .Q(R2), .clk(Write_DEST));  // open: clr
  Register #(.width(16)) register_9 (.D(DB_IN), .en(and_9_out), .Q(register_9_q), .clk(Write_DEST));  // open: clr
  Register #(.width(16)) register_10 (.D(DB_IN), .en(and_10_out), .Q(register_10_q), .clk(Write_DEST));  // open: clr
  Register #(.width(16)) register_11 (.D(DB_IN), .en(and_11_out), .Q(SP_OUT), .clk(Write_DEST));  // open: clr
  and and_12 (and_12_out, decoder_2_out3, decoder_1_out3);
  and and_13 (and_13_out, and_12_out, Write_DEST);
  Multiplexer #(.width(16)) multiplexer_1 (
    .in0(DB_IN), .in1(FLAGS_IN), .out(multiplexer_1_out), .sel(SET_F_TO_ALU));  // open: en
  and and_14 (and_14_out, decoder_2_out3, decoder_1_out0);
  and and_15 (and_15_out, decoder_2_out3, decoder_1_out1);
  and and_16 (and_16_out, decoder_2_out3, decoder_1_out2);
  or or_1 (or_1_out, and_13_out, WRITE_FLAG);
  Register #(.width(16)) register_12 (.D(DB_IN), .en(and_14_out), .Q(register_12_q), .clk(Write_DEST));  // open: clr
  Register #(.width(16)) register_13 (.D(DB_IN), .en(and_15_out), .Q(register_13_q), .clk(Write_DEST));  // open: clr
  Register #(.width(16)) register_14 (.D(DB_IN), .en(and_16_out), .Q(register_14_q), .clk(Write_DEST));  // open: clr
  Register #(.width(16)) register_15 (.D(multiplexer_1_out), .Q(FLAGS_OUT), .clk(or_1_out));  // open: en, clr
  Multiplexer #(.select(4), .width(16)) multiplexer_2 (
    .in0({16{1'b0}}), .in1(R1), .in2(R2), .in3(register_12_q), .in4(register_1_q), .in5(register_5_q),
    .in6(register_9_q), .in7(register_13_q), .in8(register_2_q), .in9(register_6_q), .in10(register_10_q),
    .in11(register_14_q), .in12(register_3_q), .in13(register_7_q), .in14(SP_OUT), .in15(FLAGS_OUT),
    .out(SRC_OUT), .sel(INS_IN[7:4]));  // open: en
  Multiplexer #(.select(4), .width(16)) multiplexer_3 (
    .in0({16{1'b0}}), .in1(R1), .in2(R2), .in3(register_12_q), .in4(register_1_q), .in5(register_5_q),
    .in6(register_9_q), .in7(register_13_q), .in8(register_2_q), .in9(register_6_q), .in10(register_10_q),
    .in11(register_14_q), .in12(register_3_q), .in13(register_7_q), .in14(SP_OUT), .in15(FLAGS_OUT),
    .out(DEST_OUT), .sel(INS_IN[3:0]));  // open: en
endmodule

module ADRR_SELECT (
  input  [15:0] PC_IN,
  input  [15:0] OP_IN,
  input  [15:0] SRC_IN,
  input  [15:0] DEST_IN,
  input  [15:0] SP_IN,
  input  PC___1,
  input  SRC_IN_2,
  input  DEST_IN_2,
  input  SP_IN_2,
  input  SP__1,
  output [15:0] OUT_ADDR
);

  wire or_1_out, or_2_out;
  wire [1:0] or_3_out;
  wire [15:0] adder_1_out, adder_2_out, multiplexer_1_out, multiplexer_2_out, multiplexer_3_out,
       subtractor_1_out, subtractor_2_out;

  or or_1 (or_1_out, SP_IN_2, SP__1);
  Subtractor #(.width(16)) subtractor_1 (.a(SP_IN), .b(16'h1), .out(subtractor_1_out));  // open: bin, bout
  or or_2 (or_2_out, SRC_IN_2, DEST_IN_2);
  Multiplexer #(.width(16)) multiplexer_1 (
    .in0(SP_IN), .in1(subtractor_1_out), .out(multiplexer_1_out), .sel(SP__1));  // open: en
  Multiplexer #(.width(16)) multiplexer_2 (
    .in0(SRC_IN), .in1(DEST_IN), .out(multiplexer_2_out), .sel(DEST_IN_2));  // open: en
  or or_3 (or_3_out[0], PC___1, or_1_out);
  or or_4 (or_3_out[1], or_2_out, or_1_out);
  Adder #(.width(16)) adder_1 (.a(PC_IN), .b(16'h1), .out(adder_1_out));  // open: cin, cout
  Adder #(.width(16)) adder_2 (.a(multiplexer_2_out), .b({1'b0, OP_IN[14:0]}), .out(adder_2_out));  // open: cin, cout
  Subtractor #(.width(16)) subtractor_2 (
    .a(multiplexer_2_out), .b({1'b0, OP_IN[14:0]}), .out(subtractor_2_out));  // open: bin, bout
  Multiplexer #(.width(16)) multiplexer_3 (
    .in0(adder_2_out), .in1(subtractor_2_out), .out(multiplexer_3_out), .sel(OP_IN[15]));  // open: en
  Multiplexer #(.select(2), .width(16)) multiplexer_4 (
    .in0(PC_IN), .in1(adder_1_out), .in2(multiplexer_3_out), .in3(multiplexer_1_out), .out(OUT_ADDR),
    .sel(or_3_out));  // open: en
endmodule

module PC_SELECT (
  input  [15:0] DB_IN,
  input  [15:0] PC_IN,
  input  [15:0] INS_IN,
  input  [15:0] FLAGS_IN,
  input  JMP,
  input  DJ,
  input  PC_2,
  input  PC_ISR,
  output [15:0] PC_OUT
);

  wire and_1_out, multiplexer_3_out, or_1_out;
  wire [15:0] adder_1_out, multiplexer_1_out, multiplexer_2_out;

  Multiplexer #(.width(16), .disabled(0), .enable("false")) multiplexer_1 (
    .in0(16'h1), .in1(16'h2), .out(multiplexer_1_out), .sel(PC_2));
  or or_1 (or_1_out, DJ, PC_ISR, and_1_out);
  and and_1 (and_1_out, JMP, multiplexer_3_out);
  Adder #(.width(16)) adder_1 (.a(PC_IN), .b(multiplexer_1_out), .out(adder_1_out));  // open: cin, cout
  Multiplexer #(.width(16)) multiplexer_2 (
    .in0(DB_IN), .in1(16'h5), .out(multiplexer_2_out), .sel(PC_ISR));  // open: en
  Multiplexer #(.select(4)) multiplexer_3 (
    .in0(FLAGS_IN[0]), .in1(FLAGS_IN[1]), .in2(FLAGS_IN[2]), .in3(FLAGS_IN[3]), .in4(FLAGS_IN[4]),
    .in5(FLAGS_IN[5]), .in6(1'b1), .out(multiplexer_3_out), .sel(INS_IN[11:8]));  // open: in7, in8, in9, in10, in11, in12, in13, in14, in15, en
  Multiplexer #(.width(16)) multiplexer_4 (
    .in0(adder_1_out), .in1(multiplexer_2_out), .out(PC_OUT), .sel(or_1_out));  // open: en
endmodule

module ALU (
  input  [15:0] X,
  input  [15:0] Y,
  input  [15:0] INS,
  input  [15:0] FLAG_IN,
  output [15:0] ANS,
  output [15:0] FLAG_OUT
);

  wire adder_1_cout, decoder_1_out9, decoder_1_out10, decoder_1_out11, decoder_1_out12, decoder_1_out15,
       or_1_out, subtractor_1_bout;
  wire [1:0] comparator_2_eq;
  wire [4:2] comparator_1_gt;
  wire [15:0] adder_1_out, and_2_out, or_2_out, subtractor_1_out, xor_1_out;
  wire [15:15] and_1_out;

  Decoder #(.select(4)) decoder_1 (
    .out9(decoder_1_out9), .out10(decoder_1_out10), .out11(decoder_1_out11), .out12(decoder_1_out12),
    .out15(decoder_1_out15), .sel(INS[11:8]));  // open: out0, out1, out2, out3, out4, out5, out6, out7, out8, out13, out14, en
  or or_1 (or_1_out, decoder_1_out9, decoder_1_out10, decoder_1_out11, decoder_1_out12);
  and and_1 (and_1_out[15], or_1_out, FLAG_IN[1]);
  Adder #(.width(16)) adder_1 (.a(X), .b(Y), .out(adder_1_out), .cin(and_1_out[15]), .cout(adder_1_cout));
  Subtractor #(.width(16)) subtractor_1 (
    .a(X), .b(Y), .out(subtractor_1_out), .bin(and_1_out[15]), .bout(subtractor_1_bout));
  assign and_2_out = X & Y;  // AND_Gate and_2, 16 bits wide
  assign or_2_out = X | Y;  // OR_Gate or_2, 16 bits wide
  assign xor_1_out = X ^ Y;  // XOR_Gate xor_1, 16 bits wide
  Comparator #(.width(16), .mode("unsigned")) comparator_1 (
    .a(Y), .b(X), .gt(comparator_1_gt[2]), .eq(comparator_1_gt[3]), .lt(comparator_1_gt[4]));
  Multiplexer #(.width(16)) multiplexer_1 (
    .in0({FLAG_IN[15:2], comparator_2_eq}), .in1({{11{1'b0}}, comparator_1_gt, FLAG_IN[1:0]}),
    .out(FLAG_OUT), .sel(decoder_1_out15));  // open: en
  Multiplexer #(.select(4)) multiplexer_2 (
    .in0(adder_1_cout), .in1(subtractor_1_bout), .in2(X[15]), .in3(X[0]), .in4(FLAG_IN[1]), .in5(FLAG_IN[1]),
    .in6(FLAG_IN[1]), .in7(adder_1_cout), .in8(subtractor_1_bout), .in9(adder_1_cout),
    .in10(subtractor_1_bout), .in11(X[15]), .in12(X[0]), .in13(FLAG_IN[1]), .in14(FLAG_IN[1]),
    .in15(FLAG_IN[1]), .out(comparator_2_eq[1]), .sel(INS[11:8]));  // open: en
  Multiplexer #(.select(4), .width(16)) multiplexer_3 (
    .in0(adder_1_out), .in1(subtractor_1_out), .in2({X[14:0], and_1_out[15]}),
    .in3({and_1_out[15], X[15:1]}), .in4(and_2_out), .in5(or_2_out), .in6(xor_1_out), .in7(adder_1_out),
    .in8(subtractor_1_out), .in9(adder_1_out), .in10(subtractor_1_out), .in11({and_1_out[15], X[15:1]}),
    .in12(and_2_out), .in13(Y), .in14(Y), .in15(Y), .out(ANS), .sel(INS[11:8]));  // open: en
  Comparator #(.width(16), .mode("unsigned")) comparator_2 (
    .a(ANS), .b({16{1'b0}}), .eq(comparator_2_eq[0]));  // open: gt, lt
endmodule

module CONTROL (
  input  [15:0] INS_IN,
  input  CLOCK,
  input  Inturupt,
  input  next_ins,
  input  Toggle_DB,
  output LOAD_PC,
  output LOAD_MEM,
  output LOAD_DEST,
  output LOAD_FLAGS,
  output LOAD_OPRAND,
  output LOAD_INS,
  output DB_ENABLED,
  output Halted,
  output ALU_TO_FLAG,
  output OPRAND_TO_ALU,
  output PC___1_TO_ADDR,
  output SP_TO_ADR,
  output SP___1_TO_ADR,
  output SRC_TO_ADR,
  output DEST_TO_ADR,
  output PC_TO_DB,
  output PC_TO_DB_W_F,
  output PC___2,
  output [3:0] DB_SELECT,
  output PC_ISR
);

  wire and_1_out, and_2_out, and_3_out, and_5_out, and_6_out, and_7_out, and_8_out, and_9_out, and_10_out,
       and_11_out, d_ff_1_qn, d_ff_2_q, d_ff_2_qn, d_ff_3_q, d_ff_3_qn, d_ff_4_q, d_ff_4_qn, decoder_1_out9,
       decoder_1_out11, decoder_1_out12, decoder_1_out13, decoder_1_out14, decoder_1_out15, decoder_2_out1,
       decoder_2_out2, decoder_2_out7, decoder_2_out8, or_1_out, or_2_out, or_3_out, or_4_out, or_5_out,
       or_6_out, or_8_out;
  wire [1:1] and_4_out;
  wire [5:0] or_9_out;
  wire [7:0] adder_1_out, multiplexer_1_out, register_1_q, rom_1_data;
  wire [11:0] rom_2_data;

  not not_1 (DB_ENABLED, d_ff_3_qn);
  or or_1 (or_1_out, CLOCK, decoder_1_out15);
  and and_1 (and_1_out, decoder_1_out11, d_ff_1_qn);
  and and_2 (and_2_out, decoder_1_out12, ~d_ff_1_qn);  // AND_Gate
  ROM rom_1 (.addr(INS_IN[15:8]), .data(rom_1_data));  // open: sel
  D_Flip_Flop d_ff_1 (.clk(or_2_out), .D(d_ff_1_qn), .Qn(d_ff_1_qn));  // open: Q, preset, en, reset
  or or_2 (or_2_out, and_1_out, and_2_out);
  and and_3 (and_3_out, or_1_out, ~Halted);  // AND_Gate
  Multiplexer #(.select(2), .width(8)) multiplexer_1 (
    .in0(adder_1_out), .in1(rom_1_data), .in2(adder_1_out), .in3(8'h1e), .out(multiplexer_1_out),
    .sel({and_4_out[1], or_9_out[5]}));  // open: en
  and and_4 (and_4_out[1], Inturupt, d_ff_1_qn);
  Register register_1 (.D(multiplexer_1_out), .Q(register_1_q), .clk(and_3_out));  // open: en, clr
  Adder adder_1 (.a(register_1_q), .b(8'h1), .out(adder_1_out));  // open: cin, cout
  or or_3 (or_3_out, decoder_1_out14, Toggle_DB);
  ROM #(.dataWidth(12)) rom_2 (
    .addr(register_1_q), .data({rom_2_data[11:8], DB_SELECT, rom_2_data[3:0]}));  // open: sel
  Decoder #(.select(4)) decoder_1 (
    .out1(or_9_out[5]), .out2(PC___1_TO_ADDR), .out4(OPRAND_TO_ALU), .out5(SRC_TO_ADR), .out6(DEST_TO_ADR),
    .out7(SP_TO_ADR), .out8(SP___1_TO_ADR), .out9(decoder_1_out9), .out10(PC_ISR), .out11(decoder_1_out11),
    .out12(decoder_1_out12), .out13(decoder_1_out13), .out14(decoder_1_out14), .out15(decoder_1_out15),
    .sel(rom_2_data[11:8]));  // open: out0, out3, en
  Decoder #(.select(4)) decoder_2 (
    .out1(decoder_2_out1), .out2(decoder_2_out2), .out3(PC_TO_DB_W_F), .out4(PC_TO_DB),
    .out7(decoder_2_out7), .out8(decoder_2_out8), .out9(ALU_TO_FLAG), .sel(rom_2_data[3:0]));  // open: out0, out5, out6, out10, out11, out12, out13, out14, out15, en
  and and_5 (and_5_out, or_9_out[5], d_ff_3_q);
  and and_6 (and_6_out, and_4_out[1], ~d_ff_2_qn);  // AND_Gate
  or or_4 (or_4_out, and_6_out, and_7_out);
  and and_7 (and_7_out, decoder_1_out13, d_ff_2_qn);
  and and_8 (and_8_out, or_3_out, d_ff_3_qn);
  or or_5 (or_5_out, and_8_out, and_9_out);
  and and_9 (and_9_out, Toggle_DB, ~d_ff_3_qn);  // AND_Gate
  or or_6 (or_6_out, DEST_TO_ADR, SRC_TO_ADR);
  D_Flip_Flop d_ff_2 (.clk(or_4_out), .D(d_ff_2_qn), .Q(d_ff_2_q), .Qn(d_ff_2_qn));  // open: preset, en, reset
  D_Flip_Flop d_ff_3 (.clk(or_5_out), .D(d_ff_3_qn), .Q(d_ff_3_q), .Qn(d_ff_3_qn));  // open: preset, en, reset
  and and_10 (and_10_out, and_5_out, d_ff_4_qn);
  and and_11 (and_11_out, next_ins, ~d_ff_4_qn);  // AND_Gate
  or or_7 (Halted, d_ff_2_q, d_ff_4_q);
  D_Flip_Flop d_ff_4 (.clk(or_8_out), .D(d_ff_4_qn), .Q(d_ff_4_q), .Qn(d_ff_4_qn));  // open: preset, en, reset
  or or_8 (or_8_out, and_10_out, and_11_out);
  or or_9 (or_9_out[0], decoder_2_out1, PC_TO_DB_W_F, PC_TO_DB, decoder_2_out7, decoder_2_out8, ALU_TO_FLAG);
  or or_10 (or_9_out[1], decoder_2_out1, decoder_2_out2);
  or or_11 (or_9_out[2], decoder_2_out8, ALU_TO_FLAG);
  Multiplexer #(.width(6)) multiplexer_2 (
    .in0({or_9_out[5], PC___1_TO_ADDR, ALU_TO_FLAG, or_9_out[2:0]}), .in1({6{1'b0}}),
    .out({LOAD_INS, LOAD_OPRAND, LOAD_FLAGS, LOAD_DEST, LOAD_MEM, LOAD_PC}), .sel(or_1_out));  // open: en
  or or_12 (PC___2, or_6_out, decoder_1_out9, OPRAND_TO_ALU);

  // Notes on the sheet:
  //   contents of rom_1 (hex, n*v repeats v):
  //   48*0 7*b d d 6*0 b 5*13 10 15*0 16 15*0 1b 58*0 3 15*0 6 15*0 9 31*0 22 27 25 11*0 1d 16*0 29
  //   contents of rom_2 (hex, n*v repeats v):
  //   0 7 100 200 508 100 200 611 100 18 100 49 100 200 449 100 200 54 100 200 953 100 200 907 762 54 100
  //   704 100 7 862 a07 b00 100 804 c00 100 d07 100 e07 100 f00
endmodule

module IO_CON (
  input  [15:0] DATA_IN,
  input  [15:0] INTURIN,
  input  [6:0] KEY_IN,
  input  [15:0] RAM_IN,
  input  CPU_SIG,
  input  [15:0] ADDR_IN,
  output WRITE_TERm,
  output WRITE_KEY,
  output WRITE_INT,
  output WRITE_MASK,
  output [15:0] DATA_OUT,
  output [6:0] TERM_OUT,
  output WRITE_RAM
);

  wire comparator_1_gt, demultiplexer_2_out1;
  wire [3:0] multiplexer_3_out;
  wire [15:0] bit_extender_2_out, multiplexer_2_out;

  Multiplexer #(.width(16)) multiplexer_1 (
    .in0(RAM_IN), .in1(multiplexer_2_out), .out(DATA_OUT), .sel(comparator_1_gt));  // open: en
  Multiplexer #(.select(4), .width(16)) multiplexer_2 (
    .in13(INTURIN), .in14(bit_extender_2_out), .out(multiplexer_2_out), .sel(multiplexer_3_out));  // open: in0, in1, in2, in3, in4, in5, in6, in7, in8, in9, in10, in11, in12, in15, en
  Demultiplexer #(.select(4)) demultiplexer_1 (
    .out12(WRITE_MASK), .out13(WRITE_INT), .out14(WRITE_KEY), .out15(WRITE_TERm), .in(demultiplexer_2_out1),
    .sel(multiplexer_3_out));  // open: out0, out1, out2, out3, out4, out5, out6, out7, out8, out9, out10, out11, en
  Demultiplexer demultiplexer_2 (
    .out0(WRITE_RAM), .out1(demultiplexer_2_out1), .in(CPU_SIG), .sel(comparator_1_gt));  // open: en
  Comparator #(.width(16), .mode("unsigned")) comparator_1 (
    .a(ADDR_IN), .b(16'hffef), .gt(comparator_1_gt));  // open: eq, lt
  Multiplexer #(.width(4)) multiplexer_3 (
    .in0(4'b0000), .in1(ADDR_IN[3:0]), .out(multiplexer_3_out), .sel(comparator_1_gt));  // open: en
  Bit_Extender #(.in_width(16), .out_width(7)) bit_extender_1 (.in(DATA_IN), .out(TERM_OUT));
  assign bit_extender_2_out = {{9{1'b0}}, KEY_IN};  // Bit_Extender bit_extender_2

  // Notes on the sheet:
  //   If the Address is in the 0xFFFx range  
  //   The top of the address range 0xFFF0 - 0xFFFF is 
  //   Reserved for memory mapped IO. This Device 
  //   Interrupts the Data flow and Save signal to Devices 
endmodule
